// Logisim project cpu_pricorisc.circ as structural Verilog: 1 circuit, main circuit full_cpu
module full_cpu (
  input  Rst
);

  wire Clk, decoder_1_out0, decoder_1_out1, decoder_1_out2, decoder_1_out3, picoriscdisassembly_1_p2, TP1_p4,
       TP1_p5, TP1_p10, TP1_p12, TP1_p16, TP1_p18, TP1_p19, TP1_p20;
  wire [1:0] TP1_p11, TP1_p13, TP1_p14, TP1_p15;
  wire [15:0] bit_extender_1_out, multiplexer_1_out, multiplexer_2_out, multiplexer_3_out, multiplexer_5_out,
       multiplexer_6_out, PC_q, picoriscdisassembly_1_p4, R0_q, R1_q, R2_q, RAM_1_p1, RAM_1_p2, TP1_p9;

  Clock u_clk (.out(Clk));
  // RAM #(.addrWidth(16), .dataWidth(16)) RAM_1: pin names not known; wires that end beside it: RAM_1_p1, RAM_1_p2
  // PicoRiscDisassembly picoriscdisassembly_1: pin names not known; wires that end beside it: 4'b1111, picoriscdisassembly_1_p2, Clk, picoriscdisassembly_1_p4
  Register #(.width(16)) IR (.D(TP1_p9), .en(TP1_p18), .clk(Clk), .Q(picoriscdisassembly_1_p4), .clr(Rst));
  // FSM_Entity #(.content("state_machine a_completer @[104,46,1200,1800]{\n	in isZero[1]   @[104,100,45,15];isNeg[1]   @[104,200,42,15];opcod[4]   @[104,300,73,15];rd[2]   @[104,400,47,15];rs[2]   @[104,500,46,15];\n	out SelM[1]   @[1269,159,35,15];SelD[2]   @[1242,218,62,15];WeReg[1]   @[1257,267,47,15];SelB[2]   @[1245,453,59,15];SelA[2]   @[1243,494,61,15];SelImm[2]   @[1224,575,80,15];cmd[3]   @[1243,642,61,15];WeMem[1]   @[1250,683,54,15];WeIR[1]   @[1268,719,36,15];selSext[1]   @[1253,756,51,15];selImmByte[1]   @[1226,797,78,15];\n	codeWidth = 6;\n	reset = Instr_mem;\n	\n	state Instr_mem[\"000000\"]:\n	 	@[139,96,30,30]\n		set SelM=\"0\";SelD=\"11\";WeReg=\"0\";SelB=\"11\";SelA=\"11\";SelImm=\"00\";cmd=\"111\";WeMem=\"0\";WeIR=\"1\";selSext=\"0\";selImmByte=\"0\";  @[139,96,30,30]	\n		goto We_IR  when default   @[376,137,50,22]; \n	state We_IR[\"000001\"]:\n	 	@[443,131,30,30]\n		set WeReg=\"0\";WeMem=\"0\";WeIR=\"1\";  @[443,131,30,30]	\n		goto S0  when (opcod==\"0000\")   @[188,314,115,22]; \n		goto S1  when (opcod==\"0001\")   @[161,377,115,22]; \n		goto S2  when (opcod==\"0010\")   @[141,465,115,22]; \n		goto S3  when (opcod==\"0011\")   @[455,482,115,22]; \n		goto S4  when (opcod==\"0100\")   @[324,589,115,22]; \n		goto S5  when (opcod==\"0101\")   @[151,718,115,22]; \n		goto S6  when (opcod==\"0110\")   @[647,645,115,22]; \n		goto S7  when (opcod==\"0111\")   @[481,771,115,22]; \n		goto S8  when (opcod==\"1000\")   @[327,943,115,22]; \n		goto S9  when (opcod==\"1001\")   @[172,1064,115,22]; \n		goto SC  when (opcod==\"1100\")   @[921,1306,115,22]; \n		goto SD  when (opcod==\"1101\")   @[931,1581,115,22]; \n		goto SA_mem  when (opcod==\"1010\")   @[231,1393,115,22]; \n		goto SB  when (opcod==\"1011\")   @[517,1411,115,22]; \n		goto SF_fin  when (opcod==\"1111\")   @[170,1660,115,22]; \n		goto Etat_vide  when default   @[590,159,50,22]; \n	state Etat_vide[\"000010\"]:\n	 	@[698,148,30,30]\n		goto inc_PC  when default   @[844,137,50,22]; \n	state inc_PC[\"000011\"]:\n	 	@[989,123,30,30]\n		set SelM=\"0\";SelD=\"11\";WeReg=\"1\";SelB=\"00\";SelA=\"11\";SelImm=\"10\";cmd=\"000\";WeMem=\"0\";WeIR=\"0\";selSext=\"0\";selImmByte=\"0\";  @[989,123,30,30]	\n		goto Instr_mem  when default   @[683,112,50,22]; \n	state S0[\"000100\"]:\n	 	@[445,229,30,30]\n		set SelM=\"0\";SelD=rd;WeReg=\"1\";SelB=\"00\";SelImm=\"11\";cmd=\"111\";WeMem=\"0\";WeIR=\"0\";selSext=\"1\";selImmByte=\"0\";  @[445,229,30,30]	\n		goto inc_PC  when default   @[617,250,50,22]; \n	state S1[\"000101\"]:\n	 	@[294,321,30,30]\n		set SelM=\"0\";SelD=rd;WeReg=\"1\";SelA=rd;SelB=rs;SelImm=\"00\";cmd=\"000\";WeMem=\"0\";WeIR=\"0\";selSext=\"0\";selImmByte=\"0\";  @[294,321,30,30]	\n		goto inc_PC  when default   @[635,295,50,22]; \n	state S2[\"000110\"]:\n	 	@[151,501,30,30]\n		set SelM=\"0\";SelD=rd;WeReg=\"1\";SelA=rs;SelImm=\"11\";cmd=\"000\";WeMem=\"0\";WeIR=\"0\";selSext=\"1\";selImmByte=\"0\";  @[151,501,30,30]	\n		goto inc_PC  when default   @[652,339,50,22]; \n	state S3[\"000111\"]:\n	 	@[601,426,30,30]\n		set SelM=\"0\";SelD=rd;WeReg=\"1\";SelA=rd;SelB=rs;SelImm=\"00\";cmd=\"001\";WeMem=\"0\";WeIR=\"0\";selSext=\"0\";selImmByte=\"0\";  @[601,426,30,30]	\n		goto inc_PC  when default   @[722,337,50,22]; \n	state S4[\"001000\"]:\n	 	@[484,522,30,30]\n		set SelM=\"0\";SelD=rd;WeReg=\"1\";SelA=rd;SelB=rs;SelImm=\"00\";cmd=\"100\";WeMem=\"0\";WeIR=\"0\";selSext=\"0\";selImmByte=\"0\";  @[484,522,30,30]	\n		goto inc_PC  when default   @[726,384,50,22]; \n	state S5[\"001001\"]:\n	 	@[265,707,30,30]\n		set SelM=\"0\";SelD=rd;WeReg=\"1\";SelA=rd;SelB=rs;SelImm=\"00\";cmd=\"011\";WeMem=\"0\";WeIR=\"0\";selSext=\"0\";selImmByte=\"0\";  @[265,707,30,30]	\n		goto inc_PC  when default   @[771,440,50,22]; \n	state S6[\"001010\"]:\n	 	@[732,711,30,30]\n		set SelM=\"0\";SelD=rd;WeReg=\"1\";SelA=rd;SelB=rs;SelImm=\"00\";cmd=\"010\";WeMem=\"0\";WeIR=\"0\";selSext=\"0\";selImmByte=\"0\";  @[732,711,30,30]	\n		goto inc_PC  when default   @[825,518,50,22]; \n	state S7[\"001011\"]:\n	 	@[546,805,30,30]\n		set SelM=\"0\";SelD=rd;WeReg=\"1\";SelA=rd;SelB=rs;SelImm=\"00\";cmd=\"110\";WeMem=\"0\";WeIR=\"0\";selSext=\"0\";selImmByte=\"0\";  @[546,805,30,30]	\n		goto inc_PC  when default   @[849,582,50,22]; \n	state S8[\"001100\"]:\n	 	@[369,978,30,30]\n		set SelM=\"0\";SelD=rd;WeReg=\"1\";SelA=rd;SelB=rs;SelImm=\"11\";cmd=\"011\";WeMem=\"0\";WeIR=\"0\";selSext=\"0\";selImmByte=\"1\";  @[369,978,30,30]	\n		goto inc_PC  when default   @[856,673,50,22]; \n	state S9[\"001101\"]:\n	 	@[282,1121,30,30]\n		set SelM=\"0\";SelD=rd;WeReg=\"1\";SelA=rd;SelB=rs;SelImm=\"11\";cmd=\"011\";WeMem=\"0\";WeIR=\"0\";selSext=\"0\";selImmByte=\"0\";  @[282,1121,30,30]	\n		goto inc_PC  when default   @[881,747,50,22]; \n	state SC[\"001110\"]:\n	 	@[1049,1258,30,30]\n		set SelM=\"0\";SelD=rd;WeReg=\"0\";SelA=rd;SelB=rs;SelImm=\"00\";cmd=\"001\";WeMem=\"0\";WeIR=\"0\";selSext=\"0\";selImmByte=\"0\";  @[1049,1258,30,30]	\n		goto inc_PC  when (/isNeg)   @[1040,1132,57,22]; \n		goto PC_imm  when isNeg   @[1084,1101,42,22]; \n	state PC_imm[\"001111\"]:\n	 	@[1132,102,30,30]\n		set SelM=\"0\";SelD=\"11\";WeReg=\"1\";SelB=\"00\";SelA=\"11\";SelImm=\"11\";cmd=\"000\";WeMem=\"0\";WeIR=\"0\";selSext=\"1\";selImmByte=\"0\";  @[1132,102,30,30]	\n		goto Instr_mem  when default   @[754,84,50,22]; \n	state SD[\"010000\"]:\n	 	@[1054,1573,30,30]\n		set SelM=\"0\";SelD=rd;WeReg=\"0\";SelA=rd;SelB=rs;SelImm=\"00\";cmd=\"001\";WeMem=\"0\";WeIR=\"0\";selSext=\"0\";selImmByte=\"0\";  @[1054,1573,30,30]	\n		goto PC_imm  when isZero   @[1124,1515,45,22]; \n		goto inc_PC  when (/isZero)   @[1000,1515,60,22]; \n	state SA_mem[\"010001\"]:\n	 	@[365,1307,30,30]\n		set WeReg=\"0\";SelB=rs;SelImm=\"00\";cmd=\"111\";WeMem=\"0\";WeIR=\"0\";  @[365,1307,30,30]	\n		goto SA_WeReg  when default   @[529,1283,50,22]; \n	state SA_WeReg[\"010010\"]:\n	 	@[591,1178,30,30]\n		set SelM=\"1\";SelD=rd;WeReg=\"1\";WeMem=\"0\";WeIR=\"0\";  @[591,1178,30,30]	\n		goto inc_PC  when default   @[892,836,50,22]; \n	state SB[\"010011\"]:\n	 	@[644,1356,30,30]\n		set SelM=\"0\";SelD=\"11\";WeReg=\"0\";SelB=rs;SelA=rd;SelImm=\"00\";cmd=\"111\";WeMem=\"1\";WeIR=\"0\";selSext=\"0\";selImmByte=\"0\";  @[644,1356,30,30]	\n		goto inc_PC  when default   @[939,921,50,22]; \n	state SF_fin[\"010100\"]:\n	 	@[326,1660,30,30]\n		set WeReg=\"0\";WeMem=\"0\";WeIR=\"0\";  @[326,1660,30,30]	\n		goto SFIN  when default   @[465,1737,50,22]; \n	state SFIN[\"010101\"]:\n	 	@[581,1681,30,30]\n		set WeReg=\"0\";WeMem=\"0\";WeIR=\"0\";  @[581,1681,30,30]	\n		goto SF_fin  when default   @[465,1673,50,22]; \n}")) TP1: pin names not known; wires that end beside it: Clk, Rst, 1'b1, TP1_p4, TP1_p5, picoriscdisassembly_1_p4[15:12], picoriscdisassembly_1_p4[11:10], picoriscdisassembly_1_p4[9:8], TP1_p9, TP1_p10, TP1_p11, TP1_p12, TP1_p13, TP1_p14, TP1_p15, TP1_p16, picoriscdisassembly_1_p2, TP1_p18, TP1_p19, TP1_p20
  // Probe on picoriscdisassembly_1_p4[11:10]
  // Probe on picoriscdisassembly_1_p4[9:8]
  // Probe on picoriscdisassembly_1_p4[7:0]
  // Probe on TP1_p9
  Multiplexer #(.width(16), .enable("false")) multiplexer_1 (
    .in0(RAM_1_p1), .in1(TP1_p9), .out(multiplexer_1_out), .sel(TP1_p10));
  // Probe on decoder_1_out0
  Decoder #(.select(2)) decoder_1 (
    .out0(decoder_1_out0), .out1(decoder_1_out1), .out2(decoder_1_out2), .out3(decoder_1_out3),
    .sel(TP1_p11), .en(TP1_p12));
  Register #(.width(16)) R0 (.D(multiplexer_1_out), .en(decoder_1_out0), .clk(Clk), .Q(R0_q), .clr(Rst));
  Register #(.width(16)) R1 (.D(multiplexer_1_out), .en(decoder_1_out1), .clk(Clk), .Q(R1_q), .clr(Rst));
  Register #(.width(16)) R2 (.D(multiplexer_1_out), .en(decoder_1_out2), .clk(Clk), .Q(R2_q), .clr(Rst));
  Register #(.width(16)) PC (.D(multiplexer_1_out), .en(decoder_1_out3), .clk(Clk), .Q(PC_q), .clr(Rst));
  Multiplexer #(.width(16), .enable("false")) multiplexer_2 (
    .in0({picoriscdisassembly_1_p4[7:0], {8{1'b0}}}), .in1({{8{1'b0}}, picoriscdisassembly_1_p4[7:0]}),
    .out(multiplexer_2_out), .sel(TP1_p20));
  assign bit_extender_1_out = {{8{picoriscdisassembly_1_p4[7]}}, picoriscdisassembly_1_p4[7:0]};  // Bit_Extender bit_extender_1
  // Probe on TP1_p13
  Multiplexer #(.width(16), .enable("false")) multiplexer_3 (
    .in0(multiplexer_2_out), .in1(bit_extender_1_out), .out(multiplexer_3_out), .sel(TP1_p19));
  // Probe on TP1_p14
  Multiplexer #(.select(2), .width(16), .enable("false")) multiplexer_4 (
    .in0(R0_q), .in1(R1_q), .in2(R2_q), .in3(PC_q), .out(RAM_1_p2), .sel(TP1_p14));
  Multiplexer #(.select(2), .width(16), .enable("false")) multiplexer_5 (
    .in0(R0_q), .in1(R1_q), .in2(R2_q), .in3(PC_q), .out(multiplexer_5_out), .sel(TP1_p13));
  // Probe on RAM_1_p2
  // Probe on multiplexer_6_out
  Multiplexer #(.select(2), .width(16), .enable("false")) multiplexer_6 (
    .in0(multiplexer_5_out), .in1({16{1'b0}}), .in2(16'h1), .in3(multiplexer_3_out), .out(multiplexer_6_out),
    .sel(TP1_p15));
  // ALU #(.width(16)) alu_1: pin names not known; wires that end beside it: RAM_1_p2, multiplexer_6_out, 1'b0, TP1_p4, TP1_p5, TP1_p16, RAM_1_p1
  // Probe on RAM_1_p1
  // Probe on TP1_p16

  // Notes on the sheet:
  //   contents of RAM_1 (hex, n*v repeats v):
  //   f 420 b100 430 b100 2 431 b100 0 433 832 b100 b200 20 a000 431 a500 c108 3100 420 b100 a600 2501
  //   b600 d0f5 433 b100 f000 b100 f000 0 0 1 15*0 f 2 7 1
endmodule
